// Logisim project BancDeRegistres.circ as structural Verilog: 2 circuits, main circuit BancRegistre
module BancRegistre (
  input  [31:0] DataIn,
  input  [2:0] RegDest,
  input  [2:0] RegB,
  input  [2:0] RegA,
  input  Clk,
  input  in_6,
  output [31:0] AOut,
  output [31:0] BOut,
  output [31:0] R0,
  output [31:0] R1,
  output [31:0] R2,
  output [31:0] R3,
  output [31:0] R4,
  output [31:0] R5,
  output [31:0] R6,
  output [31:0] R7
);

  wire decoder_1_out0, decoder_1_out1, decoder_1_out2, decoder_1_out3, decoder_1_out4, decoder_1_out5,
       decoder_1_out6, decoder_1_out7;
  wire [31:0] multiplexer_1_out, multiplexer_2_out, multiplexer_3_out, multiplexer_9_out;

  Decoder #(.select(3)) decoder_1 (
    .out0(decoder_1_out0), .out1(decoder_1_out1), .out2(decoder_1_out2), .out3(decoder_1_out3),
    .out4(decoder_1_out4), .out5(decoder_1_out5), .out6(decoder_1_out6), .out7(decoder_1_out7), .sel(RegDest));  // open: en
  Register #(.width(32)) register_1 (.D(DataIn), .en(decoder_1_out0), .clk(in_6), .Q(R0));  // open: clr
  Multiplexer #(.enable("false"), .width(32)) multiplexer_1 (
    .in0(multiplexer_9_out), .in1(DataIn), .out(multiplexer_1_out), .sel(decoder_1_out0));
  Multiplexer #(.enable("false"), .width(32)) multiplexer_2 (
    .in0(R1), .in1(DataIn), .out(multiplexer_2_out), .sel(decoder_1_out1));
  Multiplexer #(.enable("false"), .width(32)) multiplexer_3 (
    .in0(R2), .in1(DataIn), .out(multiplexer_3_out), .sel(decoder_1_out2));
  Multiplexer #(.enable("false"), .width(32)) multiplexer_4 (.in0(R3), .in1(DataIn), .out(R3), .sel(decoder_1_out3));
  Multiplexer #(.enable("false"), .width(32)) multiplexer_5 (.in0(R4), .in1(DataIn), .out(R4), .sel(decoder_1_out4));
  Multiplexer #(.enable("false"), .width(32)) multiplexer_6 (.in0(R5), .in1(DataIn), .out(R5), .sel(decoder_1_out5));
  Multiplexer #(.enable("false"), .width(32)) multiplexer_7 (.in0(R6), .in1(DataIn), .out(R6), .sel(decoder_1_out6));
  Multiplexer #(.enable("false"), .width(32)) multiplexer_8 (.in0(R7), .in1(DataIn), .out(R7), .sel(decoder_1_out7));
  Multiplexer #(.enable("false"), .width(32)) multiplexer_9 (
    .in0(multiplexer_1_out), .in1({32{1'b0}}), .out(multiplexer_9_out), .sel(in_6));
  Multiplexer #(.enable("false"), .width(32)) multiplexer_10 (
    .in0(multiplexer_2_out), .in1({32{1'b0}}), .out(R1), .sel(in_6));
  Multiplexer #(.enable("false"), .width(32)) multiplexer_11 (.in0(R3), .in1({32{1'b0}}), .out(R3), .sel(in_6));
  Multiplexer #(.enable("false"), .width(32)) multiplexer_12 (.in0(R4), .in1({32{1'b0}}), .out(R4), .sel(in_6));
  Multiplexer #(.enable("false"), .width(32)) multiplexer_13 (
    .in0(multiplexer_3_out), .in1({32{1'b0}}), .out(R2), .sel(in_6));
  Multiplexer #(.enable("false"), .width(32)) multiplexer_14 (.in0(R5), .in1({32{1'b0}}), .out(R5), .sel(in_6));
  Multiplexer #(.enable("false"), .width(32)) multiplexer_15 (.in0(R6), .in1({32{1'b0}}), .out(R6), .sel(in_6));
  Multiplexer #(.enable("false"), .width(32)) multiplexer_16 (.in0(R7), .in1({32{1'b0}}), .out(R7), .sel(in_6));
  Multiplexer #(.enable("false"), .select(3), .width(32)) multiplexer_17 (
    .in0(multiplexer_9_out), .in1(R1), .in2(R2), .in3(R3), .in4(R4), .in5(R5), .in6(R6), .in7(R7),
    .out(AOut), .sel(RegA));
  Multiplexer #(.enable("false"), .select(3), .width(32)) multiplexer_18 (
    .in0(multiplexer_9_out), .in1(R1), .in2(R2), .in3(R3), .in4(R4), .in5(R5), .in6(R6), .in7(R7),
    .out(BOut), .sel(RegB));
endmodule

module BancRegistreV2 (
  input  [2:0] RegB,
  input  [2:0] RegA,
  input  [31:0] DataIn,
  input  [2:0] RegDest,
  input  Clk,
  input  in_6,
  output [31:0] AOut,
  output [31:0] BOut,
  output [31:0] R0,
  output [31:0] R1,
  output [31:0] R2,
  output [31:0] R3,
  output [31:0] R4,
  output [31:0] R5,
  output [31:0] R6,
  output [31:0] R7
);

  wire decoder_1_out0, decoder_1_out1, decoder_1_out2, decoder_1_out3, decoder_1_out4, decoder_1_out5,
       decoder_1_out6, decoder_1_out7;

  Decoder #(.select(3)) decoder_1 (
    .out0(decoder_1_out0), .out1(decoder_1_out1), .out2(decoder_1_out2), .out3(decoder_1_out3),
    .out4(decoder_1_out4), .out5(decoder_1_out5), .out6(decoder_1_out6), .out7(decoder_1_out7), .sel(RegDest));  // open: en
  Register #(.width(32)) register_1 (.D(DataIn), .en(decoder_1_out0), .clk(Clk), .Q(R0), .clr(in_6));
  Register #(.width(32)) register_2 (.D(DataIn), .en(decoder_1_out1), .clk(Clk), .Q(R1), .clr(in_6));
  Register #(.width(32)) register_3 (.D(DataIn), .en(decoder_1_out2), .clk(Clk), .Q(R2), .clr(in_6));
  Register #(.width(32)) register_4 (.D(DataIn), .en(decoder_1_out3), .clk(Clk), .Q(R3), .clr(in_6));
  Register #(.width(32)) register_5 (.D(DataIn), .en(decoder_1_out4), .clk(Clk), .Q(R4), .clr(in_6));
  Register #(.width(32)) register_6 (.D(DataIn), .en(decoder_1_out5), .clk(Clk), .Q(R5), .clr(in_6));
  Register #(.width(32)) register_7 (.D(DataIn), .en(decoder_1_out6), .clk(Clk), .Q(R6), .clr(in_6));
  Register #(.width(32)) register_8 (.D(DataIn), .en(decoder_1_out7), .clk(Clk), .Q(R7), .clr(in_6));
  Multiplexer #(.enable("false"), .select(3), .width(32)) multiplexer_1 (
    .in0(R0), .in1(R1), .in2(R2), .in3(R3), .in4(R4), .in5(R5), .in6(R6), .in7(R7), .out(AOut), .sel(RegA));
  Multiplexer #(.enable("false"), .select(3), .width(32)) multiplexer_2 (
    .in0(R0), .in1(R1), .in2(R2), .in3(R3), .in4(R4), .in5(R5), .in6(R6), .in7(R7), .out(BOut), .sel(RegB));
endmodule
