// Logisim project Ctl_Conditional.circ as structural Verilog: 1 circuit, main circuit Conditional
module Conditional (
  input  [15:0] Instruction,
  input  Enable,
  input  Z,
  input  C,
  input  V,
  input  N,
  output [7:0] Offset,
  output Verified
);

  wire and_1_out, and_2_out, and_3_out, and_4_out, and_5_out, and_6_out, and_7_out, and_8_out, and_9_out,
       and_10_out, and_11_out, and_12_out, and_13_out, and_14_out, and_15_out, and_16_out, decoder_1_out0,
       decoder_1_out1, decoder_1_out2, decoder_1_out3, decoder_1_out4, decoder_1_out5, decoder_1_out6,
       decoder_1_out7, decoder_1_out8, decoder_1_out9, decoder_1_out10, decoder_1_out11, decoder_1_out12,
       decoder_1_out13, decoder_1_out14, decoder_1_out15, multiplexer_1_out, not_1_out, not_2_out, or_1_out,
       xnor_1_out, xor_1_out;

  Decoder #(.select(4)) decoder_1 (
    .out0(decoder_1_out0), .out1(decoder_1_out1), .out2(decoder_1_out2), .out3(decoder_1_out3),
    .out4(decoder_1_out4), .out5(decoder_1_out5), .out6(decoder_1_out6), .out7(decoder_1_out7),
    .out8(decoder_1_out8), .out9(decoder_1_out9), .out10(decoder_1_out10), .out11(decoder_1_out11),
    .out12(decoder_1_out12), .out13(decoder_1_out13), .out14(decoder_1_out14), .out15(decoder_1_out15),
    .sel(Instruction[11:8]));  // open: en
  and and_1 (and_1_out, Z, decoder_1_out0);
  and and_2 (and_2_out, ~Z, decoder_1_out1);  // AND_Gate
  and and_3 (and_3_out, C, decoder_1_out2);
  and and_4 (and_4_out, ~C, decoder_1_out3);  // AND_Gate
  and and_5 (and_5_out, N, decoder_1_out4);
  and and_6 (and_6_out, ~N, decoder_1_out5);  // AND_Gate
  and and_7 (and_7_out, V, decoder_1_out6);
  and and_8 (and_8_out, ~V, decoder_1_out7);  // AND_Gate
  and and_9 (and_9_out, C, ~Z);  // AND_Gate
  and and_10 (and_10_out, and_9_out, decoder_1_out8);
  or or_1 (or_1_out, ~C, Z);  // OR_Gate
  and and_11 (and_11_out, or_1_out, decoder_1_out9);
  xnor xnor_1 (xnor_1_out, N, V);
  and and_12 (and_12_out, xnor_1_out, decoder_1_out10);
  xor xor_1 (xor_1_out, N, V);
  and and_13 (and_13_out, xor_1_out, decoder_1_out11);
  and and_14 (and_14_out, xnor_1_out, ~Z);  // AND_Gate
  and and_15 (and_15_out, and_14_out, decoder_1_out12);
  not not_1 (not_1_out, and_14_out);
  and and_16 (and_16_out, not_1_out, decoder_1_out13);
  not not_2 (not_2_out, decoder_1_out15);
  Multiplexer #(.select(4)) multiplexer_1 (
    .in0(and_1_out), .in1(and_2_out), .in2(and_3_out), .in3(and_4_out), .in4(and_5_out), .in5(and_6_out),
    .in6(and_7_out), .in7(and_8_out), .in8(and_10_out), .in9(and_11_out), .in10(and_12_out),
    .in11(and_13_out), .in12(and_15_out), .in13(and_16_out), .in14(decoder_1_out14), .in15(not_2_out),
    .out(multiplexer_1_out), .sel(Instruction[11:8]));  // open: en
  and and_17 (Verified, multiplexer_1_out, Enable);

  assign Offset = Instruction[7:0];
endmodule
