// Logisim project Ctl_Data_Processing.circ as structural Verilog: 5 circuits, main circuit Data_Processing
module Data_Processing (
  input  Enable,
  input  [15:0] Instruction,
  output [2:0] Rd,
  output [2:0] Rn,
  output [2:0] Rm,
  output [3:0] ALU_Opcode,
  output [3:0] Flags_Update_Mask
);

  wire [1:0] rd_op_1_o, rm_op_1_o, rn_op_1_o;
  wire [2:0] multiplexer_1_out, multiplexer_2_out, multiplexer_3_out;
  wire [3:0] mask_1_nzcv;

  Rd_Op rd_op_1 (.e(Instruction[9:6]), .o(rd_op_1_o));
  Rn_Op rn_op_1 (.e(Instruction[9:6]), .o(rn_op_1_o));
  Rm_Op rm_op_1 (.e(Instruction[9:6]), .o(rm_op_1_o));
  Mask mask_1 (.e(Instruction[9:6]), .nzcv(mask_1_nzcv));
  Multiplexer #(.enable("false"), .select(2), .width(3)) multiplexer_1 (
    .in0(3'b000), .in1(Instruction[2:0]), .in2(Instruction[5:3]), .out(multiplexer_1_out), .sel(rd_op_1_o));  // open: in3
  Multiplexer #(.enable("false"), .select(2), .width(3)) multiplexer_2 (
    .in0(3'b000), .in1(Instruction[2:0]), .in2(Instruction[5:3]), .out(multiplexer_2_out), .sel(rn_op_1_o));  // open: in3
  Multiplexer #(.enable("false"), .select(2), .width(3)) multiplexer_3 (
    .in0(3'b000), .in1(Instruction[2:0]), .in2(Instruction[5:3]), .out(multiplexer_3_out), .sel(rm_op_1_o));  // open: in3
  Multiplexer #(.enable("false"), .width(3)) multiplexer_4 (
    .in0(3'b000), .in1(multiplexer_1_out), .out(Rd), .sel(Enable));
  Multiplexer #(.enable("false"), .width(3)) multiplexer_5 (
    .in0(3'b000), .in1(multiplexer_2_out), .out(Rn), .sel(Enable));
  Multiplexer #(.enable("false"), .width(3)) multiplexer_6 (
    .in0(3'b000), .in1(multiplexer_3_out), .out(Rm), .sel(Enable));
  Multiplexer #(.enable("false"), .width(4)) multiplexer_7 (
    .in0(4'b0000), .in1(Instruction[9:6]), .out(ALU_Opcode), .sel(Enable));
  Multiplexer #(.enable("false"), .width(4)) multiplexer_8 (
    .in0(4'b0000), .in1(mask_1_nzcv), .out(Flags_Update_Mask), .sel(Enable));

  // Notes on the sheet:
  //   Note 2: RSB instruction has Rn as 1st operand.
  //   MUL instruction has Rn as 1st operand and Rdm as 2nd operand
  //   For simplification purposes, Rm is used for 1st operand both here and in the ALU. Order for flags : NZCV
  //   Note: instructions that does not save the result will still have the second operand as the destination register, the ALU will copy the second register to the destination register
  //   Pull output low on Enable = 0
endmodule

module Rd_Op (
  input  [3:0] e,
  output [1:0] o
);

  wire and_1_out, not_1_out, not_2_out;

  not not_1 (not_1_out, e[3]);
  not not_2 (not_2_out, e[1]);
  and and_1 (and_1_out, not_2_out, e[0]);
  or or_1 (o[0], not_1_out, and_1_out, e[2]);

  assign o[1] = 1'b0;
endmodule

module Rn_Op (
  input  [3:0] e,
  output [1:0] o
);

  wire and_2_out, not_1_out, not_2_out, not_3_out, not_4_out;

  not not_1 (not_1_out, e[3]);
  not not_2 (not_2_out, e[2]);
  not not_3 (not_3_out, e[1]);
  not not_4 (not_4_out, e[0]);
  and and_1 (o[1], e[3], not_3_out, e[0]);
  or or_1 (o[0], not_1_out, not_4_out, and_2_out);
  and and_2 (and_2_out, not_2_out, e[1]);
endmodule

module Rm_Op (
  input  [3:0] e,
  output [1:0] o
);

  wire not_1_out, not_2_out, not_3_out;

  not not_1 (not_1_out, e[3]);
  not not_2 (not_2_out, e[1]);
  not not_3 (not_3_out, e[0]);
  or or_1 (o[1], not_1_out, not_3_out, e[1]);
  and and_1 (o[0], e[3], e[2], not_2_out, e[0]);
endmodule

module Mask (
  input  [3:0] e,
  output [3:0] nzcv
);

  wire and_1_out, and_2_out, and_3_out, and_4_out, not_1_out, not_2_out, not_3_out, not_4_out;

  not not_1 (not_1_out, e[3]);
  not not_2 (not_2_out, e[2]);
  not not_3 (not_3_out, e[1]);
  not not_4 (not_4_out, e[0]);
  or or_1 (nzcv[1], not_1_out, not_2_out, not_4_out, e[1]);
  and and_1 (and_1_out, not_1_out, e[2], not_3_out, e[0]);
  and and_2 (and_2_out, not_1_out, e[2], e[1], not_4_out);
  and and_3 (and_3_out, e[3], not_2_out, e[0]);
  and and_4 (and_4_out, e[3], not_2_out, e[1]);
  or or_2 (nzcv[0], and_1_out, and_2_out, and_3_out, and_4_out);

  assign nzcv[3:2] = 2'b11;
endmodule
