// Logisim project Ctl_Flags_APSR.circ as structural Verilog: 1 circuit, main circuit Flags_APSR
module Flags_APSR (
  input  [3:0] Flags_In,
  input  [3:0] Update_Mask,
  input  Clk,
  input  Rst,
  output [3:0] Flags_Out
);

  wire [3:0] multiplexer_1_out;

  Multiplexer #(.enable("false"), .select(4), .width(4)) multiplexer_1 (
    .in0(Flags_Out), .in1({Flags_Out[3:1], Flags_In[0]}), .in2({Flags_Out[3:2], Flags_In[1], Flags_Out[1]}),
    .in3({Flags_Out[3:2], Flags_In[1:0]}), .in4({Flags_Out[3], Flags_In[2], Flags_Out[1:0]}),
    .in5({Flags_Out[3], Flags_In[2], Flags_Out[1], Flags_In[0]}),
    .in6({Flags_Out[3], Flags_In[2:1], Flags_Out[0]}), .in7({Flags_Out[3], Flags_In[2:0]}),
    .in8({Flags_In[3], Flags_Out[2:0]}), .in9({Flags_In[3], Flags_Out[2:1], Flags_In[0]}),
    .in10({Flags_In[3], Flags_Out[2], Flags_In[1], Flags_Out[0]}),
    .in11({Flags_In[3], Flags_Out[2], Flags_In[1:0]}), .in12({Flags_In[3:2], Flags_Out[1:0]}),
    .in13({Flags_In[3:2], Flags_Out[1], Flags_In[0]}), .in14({Flags_In[3:1], Flags_Out[0]}), .in15(Flags_In),
    .out(multiplexer_1_out), .sel(Update_Mask));
  Register #(.width(4)) register_1 (.D(multiplexer_1_out), .clk(Clk), .Q(Flags_Out), .clr(Rst));  // open: en

  // Other names for the same wires on the sheet: V = Flags_In[0]; C = Flags_In[1]; Z = Flags_In[2]; N = Flags_In[3];
  //   OldV = Flags_Out[0]; OldC = Flags_Out[1]; OldZ = Flags_Out[2]; OldN = Flags_Out[3]
endmodule
