// Logisim project Ctl_Load_Store.circ as structural Verilog: 1 circuit, main circuit Load_Store
module Load_Store (
  input  Enable,
  input  [15:0] Instruction,
  input  [31:0] Stack_Pointer,
  input  Clk,
  input  Reset,
  output Store,
  output Load,
  output PC_Hold,
  output [2:0] Rmd,
  output [31:0] RAM_Addr
);

  wire and_1_out, and_2_out, and_3_out, d_ff_1_q, demultiplexer_1_out0, demultiplexer_1_out1, not_1_out;
  wire [31:0] adder_1_out, bit_extender_1_out;

  assign bit_extender_1_out = {{24{1'b0}}, Instruction[7:0]};  // Bit_Extender bit_extender_1
  Adder #(.width(32)) adder_1 (.a(Stack_Pointer), .b(bit_extender_1_out), .out(adder_1_out));  // open: cin, cout
  and and_1 (and_1_out, Enable, Clk);
  and and_2 (and_2_out, demultiplexer_1_out1, and_1_out);
  Demultiplexer #(.enable("true")) demultiplexer_1 (
    .out0(demultiplexer_1_out0), .out1(demultiplexer_1_out1), .in(1'b1), .sel(Instruction[11]));  // open: en
  D_Flip_Flop d_ff_1 (.D(not_1_out), .clk(and_2_out), .Q(d_ff_1_q), .reset(Reset));  // open: Qn, preset
  not not_1 (not_1_out, d_ff_1_q);
  and and_3 (and_3_out, demultiplexer_1_out1, d_ff_1_q);
  Multiplexer #(.enable("true")) multiplexer_1 (
    .in0(1'b0), .in1(demultiplexer_1_out0), .out(Store), .sel(Enable));  // open: en
  Multiplexer #(.enable("true")) multiplexer_2 (
    .in0(1'b0), .in1(demultiplexer_1_out1), .out(Load), .sel(Enable));  // open: en
  Multiplexer #(.enable("true")) multiplexer_3 (.in0(1'b0), .in1(and_3_out), .out(PC_Hold), .sel(Enable));  // open: en
  Multiplexer #(.enable("true"), .width(3)) multiplexer_4 (
    .in0(3'b000), .in1(Instruction[10:8]), .out(Rmd), .sel(Enable));  // open: en
  Multiplexer #(.enable("true"), .width(32)) multiplexer_5 (
    .in0({32{1'b0}}), .in1(adder_1_out), .out(RAM_Addr), .sel(Enable));  // open: en

  // Notes on the sheet:
  //   Instruction: pull=down
  //   Delay load and hold PC for 1 cycle for the RAM to send out requested data 
endmodule
