// Logisim project Ctl_Shift_Add_Sub_Mov.circ as structural Verilog: 5 circuits, main circuit Shift_Add_Sub_Mov
module Shift_Add_Sub_Mov (
  input  Enable,
  input  [15:0] Instruction,
  output Carry,
  output Imm32_Enable,
  output [4:0] Imm5,
  output [31:0] Imm32,
  output [3:0] ALU_Opcode,
  output [2:0] Rm,
  output [2:0] Rn,
  output [2:0] Rd,
  output [3:0] Flags_Update_Mask
);

  wire carryin_1_carry, imm32_enabler_1_enable;
  wire [2:0] Rd_t, Rm_t, Rn_t;
  wire [3:0] ALU_Opcode_t, sams_flags_mask_1_mask;
  wire [4:0] Imm5_t;
  wire [31:0] bit_extender_1_out, bit_extender_2_out, Imm32_t;

  Multiplexer #(.enable("false"), .select(5), .width(5)) multiplexer_1 (
    .in0(Instruction[10:6]), .in1(Instruction[10:6]), .in2(Instruction[10:6]), .in3(Instruction[10:6]),
    .in4(Instruction[10:6]), .in5(Instruction[10:6]), .in6(Instruction[10:6]), .in7(Instruction[10:6]),
    .in8(Instruction[10:6]), .in9(Instruction[10:6]), .in10(Instruction[10:6]), .in11(Instruction[10:6]),
    .in12({5{1'b0}}), .in13({5{1'b0}}), .in14({5{1'b0}}), .in15({5{1'b0}}), .in16({5{1'b0}}),
    .in17({5{1'b0}}), .in18({5{1'b0}}), .in19({5{1'b0}}), .in20({5{1'b0}}), .in21({5{1'b0}}),
    .in22({5{1'b0}}), .in23({5{1'b0}}), .in24({5{1'b0}}), .in25({5{1'b0}}), .in26({5{1'b0}}),
    .in27({5{1'b0}}), .in28({5{1'b0}}), .in29({5{1'b0}}), .in30({5{1'b0}}), .in31({5{1'b0}}), .out(Imm5_t),
    .sel(Instruction[13:9]));
  SAMS_Opcode sams_opcode_1 (.opCode(Instruction[13:9]), .ALU_Opcode(ALU_Opcode_t));
  Multiplexer #(.enable("false"), .select(5), .width(3)) multiplexer_2 (
    .in0(Instruction[2:0]), .in1(Instruction[2:0]), .in2(Instruction[2:0]), .in3(Instruction[2:0]),
    .in4(Instruction[2:0]), .in5(Instruction[2:0]), .in6(Instruction[2:0]), .in7(Instruction[2:0]),
    .in8(Instruction[2:0]), .in9(Instruction[2:0]), .in10(Instruction[2:0]), .in11(Instruction[2:0]),
    .in12(Instruction[2:0]), .in13(Instruction[2:0]), .in14(Instruction[2:0]), .in15(Instruction[2:0]),
    .in16(Instruction[10:8]), .in17(Instruction[10:8]), .in18(Instruction[10:8]), .in19(Instruction[10:8]),
    .in20(Instruction[10:8]), .in21(Instruction[10:8]), .in22(Instruction[10:8]), .in23(Instruction[10:8]),
    .in24(Instruction[10:8]), .in25(Instruction[10:8]), .in26(Instruction[10:8]), .in27(Instruction[10:8]),
    .in28(Instruction[10:8]), .in29(Instruction[10:8]), .in30(Instruction[10:8]), .in31(Instruction[10:8]),
    .out(Rd_t), .sel(Instruction[13:9]));
  Multiplexer #(.enable("false"), .select(5), .width(3)) multiplexer_3 (
    .in0(Instruction[5:3]), .in1(Instruction[5:3]), .in2(Instruction[5:3]), .in3(Instruction[5:3]),
    .in4(Instruction[5:3]), .in5(Instruction[5:3]), .in6(Instruction[5:3]), .in7(Instruction[5:3]),
    .in8(Instruction[5:3]), .in9(Instruction[5:3]), .in10(Instruction[5:3]), .in11(Instruction[5:3]),
    .in12(Instruction[8:6]), .in13(3'b000), .in14(3'b000), .in15(3'b000), .in16(3'b000), .in17(3'b000),
    .in18(3'b000), .in19(3'b000), .in20(3'b000), .in21(3'b000), .in22(3'b000), .in23(3'b000), .in24(3'b000),
    .in25(3'b000), .in26(3'b000), .in27(3'b000), .in28(3'b000), .in29(3'b000), .in30(3'b000), .in31(3'b000),
    .out(Rm_t), .sel(Instruction[13:9]));
  Multiplexer #(.enable("false"), .select(5), .width(3)) multiplexer_4 (
    .in0(3'b000), .in1(3'b000), .in2(3'b000), .in3(3'b000), .in4(3'b000), .in5(3'b000), .in6(3'b000),
    .in7(3'b000), .in8(3'b000), .in9(3'b000), .in10(3'b000), .in11(3'b000), .in12(Instruction[5:3]),
    .in13(Instruction[5:3]), .in14(Instruction[5:3]), .in15(Instruction[5:3]), .in16(3'b000), .in17(3'b000),
    .in18(3'b000), .in19(3'b000), .in20(3'b000), .in21(3'b000), .in22(3'b000), .in23(3'b000), .in24(3'b000),
    .in25(3'b000), .in26(3'b000), .in27(3'b000), .in28(3'b000), .in29(3'b000), .in30(3'b000), .in31(3'b000),
    .out(Rn_t), .sel(Instruction[13:9]));
  CarryIn carryin_1 (.Opcode(Instruction[13:9]), .Carry(carryin_1_carry));
  Imm32_Enabler imm32_enabler_1 (.Opcode(Instruction[13:9]), .enable(imm32_enabler_1_enable));
  assign bit_extender_1_out = {{29{Instruction[8]}}, Instruction[8:6]};  // Bit_Extender bit_extender_1
  assign bit_extender_2_out = {{24{Instruction[7]}}, Instruction[7:0]};  // Bit_Extender bit_extender_2
  Multiplexer #(.enable("false")) multiplexer_5 (.in0(1'b0), .in1(carryin_1_carry), .out(Carry), .sel(Enable));
  Multiplexer #(.enable("false")) multiplexer_6 (
    .in0(1'b0), .in1(imm32_enabler_1_enable), .out(Imm32_Enable), .sel(Enable));
  Multiplexer #(.enable("false"), .width(5)) multiplexer_7 (.in0({5{1'b0}}), .in1(Imm5_t), .out(Imm5), .sel(Enable));
  SAMS_flags_mask sams_flags_mask_1 (.Opcode(Instruction[13:9]), .mask(sams_flags_mask_1_mask));
  Multiplexer #(.enable("false"), .select(5), .width(32)) multiplexer_8 (
    .in0({32{1'b0}}), .in1({32{1'b0}}), .in2({32{1'b0}}), .in3({32{1'b0}}), .in4({32{1'b0}}),
    .in5({32{1'b0}}), .in6({32{1'b0}}), .in7({32{1'b0}}), .in8({32{1'b0}}), .in9({32{1'b0}}),
    .in10({32{1'b0}}), .in11({32{1'b0}}), .in12({32{1'b0}}), .in13(bit_extender_1_out),
    .in14(bit_extender_1_out), .in15(bit_extender_1_out), .in16(bit_extender_2_out),
    .in17(bit_extender_2_out), .in18(bit_extender_2_out), .in19(bit_extender_2_out),
    .in20(bit_extender_2_out), .in21(bit_extender_2_out), .in22(bit_extender_2_out),
    .in23(bit_extender_2_out), .in24(bit_extender_2_out), .in25(bit_extender_2_out),
    .in26(bit_extender_2_out), .in27(bit_extender_2_out), .in28(bit_extender_2_out),
    .in29(bit_extender_2_out), .in30(bit_extender_2_out), .in31(bit_extender_2_out), .out(Imm32_t),
    .sel(Instruction[13:9]));
  Multiplexer #(.enable("false"), .width(32)) multiplexer_9 (
    .in0({32{1'b0}}), .in1(Imm32_t), .out(Imm32), .sel(Enable));
  Multiplexer #(.enable("false"), .width(4)) multiplexer_10 (
    .in0(4'b0000), .in1(ALU_Opcode_t), .out(ALU_Opcode), .sel(Enable));
  Multiplexer #(.enable("false"), .width(3)) multiplexer_11 (.in0(3'b000), .in1(Rm_t), .out(Rm), .sel(Enable));
  Multiplexer #(.enable("false"), .width(3)) multiplexer_12 (.in0(3'b000), .in1(Rn_t), .out(Rn), .sel(Enable));
  Multiplexer #(.enable("false"), .width(3)) multiplexer_13 (.in0(3'b000), .in1(Rd_t), .out(Rd), .sel(Enable));
  Multiplexer #(.enable("false"), .width(4)) multiplexer_14 (
    .in0(4'b0000), .in1(sams_flags_mask_1_mask), .out(Flags_Update_Mask), .sel(Enable));

  // Other names for the same wires on the sheet: Imm8[7:0] = Instruction[7:0]; RdA[2:0] = Instruction[2:0];
  //   Rm_Rn[2:0] = Instruction[5:3]; Imm3[2:0] = Instruction[8:6]; Imm5bits[4:0] = Instruction[10:6];
  //   Rm2[2:0] = Instruction[8:6]; RdB[2:0] = Instruction[10:8]; Opcode[4:0] = Instruction[13:9]

  // Notes on the sheet:
  //   Pull output low on Enable = 0
  //   Note: ALU uses Rn register for shifts. Use Rn instead of Rm for shifts (immediate) here too
  //   Note 3: Imm32_Enable forces the use of the immediate for Rm register
  //   Note 2: MOV uses RSB ALU opcode with Imm8 reversed so that it is copied to output register
  //   only ADD and SUB use Rm
endmodule

module SAMS_Opcode (
  input  [4:0] opCode,
  output [3:0] ALU_Opcode
);

  wire and_2_out, and_3_out, and_4_out, and_5_out, and_6_out, not_1_out, not_2_out, not_3_out;

  not not_1 (not_1_out, opCode[4]);
  not not_2 (not_2_out, opCode[3]);
  not not_3 (not_3_out, opCode[2]);
  and and_1 (ALU_Opcode[3], opCode[4], not_2_out);
  and and_2 (and_2_out, not_1_out, not_2_out);
  and and_3 (and_3_out, opCode[2], opCode[0]);
  or or_1 (ALU_Opcode[1], and_2_out, and_3_out, and_4_out);
  and and_4 (and_4_out, opCode[4], opCode[2]);
  and and_5 (and_5_out, not_1_out, not_2_out, opCode[2]);
  or or_2 (ALU_Opcode[0], and_5_out, and_6_out);
  and and_6 (and_6_out, opCode[4], not_2_out, not_3_out);

  assign ALU_Opcode[2] = opCode[3];
endmodule

module SAMS_flags_mask (
  input  [4:0] Opcode,
  output [3:0] mask
);

  wire and_1_out, not_1_out;

  not not_1 (not_1_out, Opcode[4]);
  or or_1 (mask[1], not_1_out, Opcode[2], Opcode[3]);
  or or_2 (mask[0], Opcode[3], and_1_out);
  and and_1 (and_1_out, Opcode[4], Opcode[2]);

  assign mask[3:2] = 2'b11;
endmodule

module CarryIn (
  input  [4:0] Opcode,
  output Carry
);

  wire and_1_out, and_2_out;

  and and_1 (and_1_out, Opcode[3], Opcode[2], Opcode[0]);
  or or_1 (Carry, and_1_out, and_2_out);
  and and_2 (and_2_out, Opcode[4], Opcode[3], Opcode[2]);
endmodule

module Imm32_Enabler (
  input  [4:0] Opcode,
  output enable
);

  wire and_1_out;

  and and_1 (and_1_out, Opcode[3], Opcode[2]);
  or or_1 (enable, and_1_out, Opcode[4]);
endmodule
